// Logisim project aiAlu.circ as structural Verilog
module MUX_4_inputs (
  input  [1:0] Select,
  input  [3:0] Data,
  output Output
);

  wire and_1_out, and_2_out, and_3_out, and_4_out, not_1_out, not_2_out, not_3_out, not_4_out;

  and and_1 (and_1_out, Select[0], Select[1], Data[3]);
  not not_1 (not_1_out, Select[0]);
  and and_2 (and_2_out, not_1_out, Select[1], Data[2]);
  and and_3 (and_3_out, Select[0], not_2_out, Data[1]);
  not not_2 (not_2_out, Select[1]);
  not not_3 (not_3_out, Select[0]);
  and and_4 (and_4_out, not_3_out, not_4_out, Data[0]);
  not not_4 (not_4_out, Select[1]);
  or or_1 (Output, and_1_out, and_2_out, and_3_out, and_4_out);
endmodule

module fullAdder (
  input  A,
  input  B,
  input  Carry_In,
  output Output,
  output Carry_Out
);

  wire and_1_out, and_2_out, and_3_out, xor_1_out;

  xor xor_1 (xor_1_out, A, B);
  and and_1 (and_1_out, A, B);
  and and_2 (and_2_out, B, Carry_In);
  and and_3 (and_3_out, A, Carry_In);
  xor xor_2 (Output, xor_1_out, Carry_In);
  or or_1 (Carry_Out, and_1_out, and_2_out, and_3_out);
endmodule
